# Fritzing sketch 接线图 (saved by Fritzing 0.9.3b)
breadboards: 1

parts:
  红外测温 = MLX90614 [package=to-39]
  超声波测距 = hc-sr04
  OLED128*64_9_96 = Grove OLED 128x96
  元件2 = ws2812b [package="smd 2812b"]
  元件3 = ws2812b [package="smd 2812b"]
  元件4 = ws2812b [package="smd 2812b"]
  元件5 = ws2812b [package="smd 2812b"]
  元件6 = ws2812b [package="smd 2812b"]
  元件7 = ws2812b [package="smd 2812b"]
  元件8 = ws2812b [package="smd 2812b"]
  元件9 = ws2812b [package="smd 2812b"]
  元件10 = ws2812b [package="smd 2812b"]
  元件11 = ws2812b [package="smd 2812b"]
  元件12 = ws2812b [package="smd 2812b"]
  元件13 = ws2812b [package="smd 2812b"]
  元件14 = ws2812b [package="smd 2812b"]
  元件15 = ws2812b [package="smd 2812b"]
  元件16 = ws2812b [package="smd 2812b"]
  4*4_RGBLED = ws2812b [package="smd 2812b"]
  元件18 = Arduino Uno (Rev3)
  无源蜂鸣器 = Piezo Speaker

nets:
  N1: 红外测温.SCL_VZ, OLED128*64_9_96.SCL, 元件18.A5/SCL
  N2: 红外测温.PWM_SDA, OLED128*64_9_96.SDA, 元件18.A4/SDA
  VDD: 红外测温.VDD, 超声波测距.VCC, OLED128*64_9_96.VCC, 元件2.VDD, 元件3.VDD, 元件4.VDD, 元件5.VDD, 元件6.VDD, 元件7.VDD, 元件8.VDD, 元件9.VDD, 元件10.VDD, 元件11.VDD, 元件12.VDD, 元件13.VDD, 元件14.VDD, 元件15.VDD, 元件16.VDD, 4*4_RGBLED.VDD, 元件18.5V
  VSS: 红外测温.VSS, 超声波测距.GND, OLED128*64_9_96.GND, 元件2.VSS, 元件3.VSS, 元件4.VSS, 元件5.VSS, 元件6.VSS, 元件7.VSS, 元件8.VSS, 元件9.VSS, 元件10.VSS, 元件11.VSS, 元件12.VSS, 元件13.VSS, 元件14.VSS, 元件15.VSS, 元件16.VSS, 4*4_RGBLED.VSS, 元件18.GND, 无源蜂鸣器.pin1
  N3: 超声波测距.Trig, 元件18.D8
  N4: 超声波测距.Echo, 元件18.D7
  N5: 元件2.DOUT, 元件3.DIN
  N6: 元件2.DIN, 元件13.DOUT
  N7: 元件3.DOUT, 元件4.DIN
  N8: 元件4.DOUT, 元件5.DIN
  N9: 元件5.DOUT, 元件6.DIN
  N10: 元件6.DOUT, 元件7.DIN
  N11: 元件7.DOUT, 元件8.DIN
  N12: 元件8.DOUT, 元件9.DIN
  N13: 元件10.DOUT, 元件11.DIN
  N14: 元件10.DIN, 4*4_RGBLED.DOUT
  N15: 元件11.DOUT, 元件12.DIN
  N16: 元件12.DOUT, 元件13.DIN
  N17: 元件14.DOUT, 元件15.DIN
  N18: 元件14.DIN, 元件18.D4
  N19: 元件15.DOUT, 元件16.DIN
  N20: 元件16.DOUT, 4*4_RGBLED.DIN
  N21: 元件18.D3_PWM, 无源蜂鸣器.pin2

notes:
  RGB LED4*4接D4
  无源蜂鸣器接D3
  OLED 128*64 I²C
  SCL接A5
  SDL接A4
  超声波测距
  Echo接D7
  Trig接D8
  红外测温I²C
  SCL接A5
  SDL接A4
